# Fritzing sketch pizero (saved by Fritzing 0.9.2b)
circuit board: 6.5cm x 3cm
breadboards: 1

parts:
  J1 = double row rounded female pin header, 40 pins [form="♀ (female rounded)"]
  S2 = female pin header, 3 pins [form="♀ (female)"]
  4_7kΩ = Resistor [tolerance=±5% resistance=4.7k package="1206 [SMD]"]
  S1 = female pin header, 3 pins [form="♀ (female)"]
  S3 = female pin header, 3 pins [form="♀ (female)"]
  S4 = female pin header, 3 pins [form="♀ (female)"]
  S5 = female pin header, 3 pins [form="♀ (female)"]

nets:
  N1: J1.pin1, S2.pin1, 4_7kΩ.Pin_0, S1.pin1, S3.pin1, S4.pin1, S5.pin1
  N2: J1.pin4, S2.pin2, 4_7kΩ.Pin_1, S1.pin2, S3.pin2, S4.pin2, S5.pin2
  N3: J1.pin5, S2.pin3, S1.pin3, S3.pin3, S4.pin3, S5.pin3

notes:
  temperature-machine
  v1.1
  ©toby weston 2016
  VDD
  DQ
  GND
  multiple sensor add-on board
  1
  baddotrobot.com
